# Fritzing sketch EnvironmentalChamber (saved by Fritzing 0.9.10b)

parts:
  Q1 = MOSFET-NCHANNEL [package=to220v]
  Q2 = MOSFET-NCHANNEL [package=to220v]
  RY1 = SSR-40DA [part_number=SSR-40DA]
  J1 = XT60 Connector female [package=THT]
  J2 = XT60 Connector male [package=THT]
  J3 = JST-2Pin-M [package=THT]
  J4 = JST-2Pin-F [package=THT]  # not connected
  J5 = JST-2Pin-F [package=THT]
  J6 = JST-2Pin-M [package=THT]  # not connected
  J7 = XT60 Connector female [package=THT]  # not connected
  J8 = XT60 Connector male [package=THT]  # not connected
  Part2 = Adafruit Thermocouple Amplifier MAX31855 [part_number="Adafruit #269"]
  Part3 = Arduino Leonardo (Rev3b)
  OLED_I2C1 = OLED 128x64 I2C Monochrome Display
  R1 = Resistor [tolerance=±5% resistance=10k package="2010 [SMD]"]
  R2 = Resistor [tolerance=±5% resistance=10k package="2010 [SMD]"]

nets:
  N1: Q1.G, Part3.D13_PWM, R1.Pin_0
  GND: Q1.S, Q2.S, J2.GND, Part2.GND, Part3.GND, OLED_I2C1.GND
  N2: Q2.G, Part3.D9_PWM/A9, R2.Pin_0
  N3: RY1.Pin_3, J5.VCC
  N4: RY1.Pin_4, J5.GND
  VCC: J1.VCC, J2.VCC
  N5: J3.VCC, Part3.D12/A11
  VIN: Part2.VIN, Part3.5V, OLED_I2C1.VDD
  N6: Part2.CS, Part3.D10_PWM/A10
  N7: Part3.SDA, OLED_I2C1.SDA
  N8: Part3.SCL, OLED_I2C1.SCK

notes:
  12V Power Supply (min 5A)
  Heater
  Fan of Heater
  Compressor
  (AC, Careful)
  Thermocouple

custom parts:
  SSR-40DA: Solid State Relay, SSR-40DA Links: SSR-40DA Datasheet
  XT60 Connector female: Yellow XT60 connector for high current loads up to 40A female
  XT60 Connector male: Yellow XT60 connector for high current loads up to 40A male
  JST-2Pin-M: 2 Pin 2 - 4Amp JST connector fround on RC quads
  JST-2Pin-F: 2 Pin 2 - 4Amp JST connector fround on RC quads
  Adafruit Thermocouple Amplifier MAX31855: Thermocouples are very sensitive, requiring a good amplifier with a cold-compensation reference. The MAX31855K does everything for you, and can be easily interfaced with any microcontroller, even one without an analog input. This breakout board has the chip itself, a 3.3V regulator with 10uF bypass capacitors and level shifting circuitry, all assembled and tested. Comes with a 2 pin terminal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
